// Digital circuit 3 Bit ALU.dig as structural Verilog
module _3_Bit_ALU (
  input  [2:0] A_2_0,
  input  [1:0] OP_1_0,
  input  [2:0] B_2_0,
  output [2:0] R_2_0
);

  wire [2:0] _3_bit_adder_1_r_2_0, _3_bit_or_1_r_2_0, _3_bit_rol_1_r_2_0;

  _3_Bit_Adder _3_bit_adder_1 (.A_2_0(A_2_0), .B_2_0(B_2_0), .R_2_0(_3_bit_adder_1_r_2_0));  // open: Cout
  _3_Bit_OR _3_bit_or_1 (.A_2_0(A_2_0), .B_2_0(B_2_0), .R_2_0(_3_bit_or_1_r_2_0));
  _3_Bit_ROL _3_bit_rol_1 (.A_2_0(A_2_0), .B_2_0(B_2_0), .R_2_0(_3_bit_rol_1_r_2_0));
  Multiplexer #(.Selector_Bits(2), .Bits(3)) multiplexer_1 (
    .sel(OP_1_0), .in_0(_3_bit_adder_1_r_2_0), .in_1(_3_bit_or_1_r_2_0), .in_2(_3_bit_rol_1_r_2_0),
    .in_3(3'b000), .out(R_2_0));

  // Other names for the same wires on the sheet: A[2:0] = A_2_0; B[2:0] = B_2_0
endmodule
