// Digital circuit 3 Bit Adder.dig as structural Verilog
module _3_Bit_Adder (
  input  [2:0] A_2_0,
  input  [2:0] B_2_0,
  output [2:0] R_2_0,
  output Cout
);

  wire fa_2_cout, fa_3_cout;

  FA fa_1 (.X(A_2_0[2]), .Y(B_2_0[2]), .Cin(fa_2_cout), .S(R_2_0[2]), .Cout(Cout));
  FA fa_2 (.X(A_2_0[1]), .Y(B_2_0[1]), .Cin(fa_3_cout), .S(R_2_0[1]), .Cout(fa_2_cout));
  FA fa_3 (.X(A_2_0[0]), .Y(B_2_0[0]), .Cin(1'b0), .S(R_2_0[0]), .Cout(fa_3_cout));
endmodule
