// Digital circuit 3 Bit CPU (Final).dig as structural Verilog
module _3_Bit_CPU__Final (
  input  [3:0] WR_3_0,
  input  [14:0] WRD_14_0,
  input  WE,
  input  CLK,
  input  PC_EN,
  input  [3:0] RA2_3_0,
  input  ZF,
  input  SF,
  output [14:0] RD2_14_0,
  output [2:0] WR_2_0,
  output [2:0] R1_2_0,
  output [2:0] R2_2_0,
  output [2:0] A_2_0,
  output [2:0] B_2_0,
  output [2:0] R_2_0,
  output [3:0] JMP_ADDR_3_0
);

  wire CPU_CLK, IMM_Sel, JMP_SEL, REG_EN;
  wire [1:0] Op;
  wire [2:0] _3_bit_register_set_1_b_2_0;
  wire [3:0] _4_bit_pc_adder_1_o_3_0, _4_bit_program_counter_1_o_3_0, multiplexer_1_out;
  wire [4:0] Don_t_Care;
  wire [14:11] _9x15_sram_1_rd1_14_0;

  Multiplexer #(.Bits(4)) multiplexer_1 (
    .sel(JMP_SEL), .in_0(_4_bit_pc_adder_1_o_3_0), .in_1(JMP_ADDR_3_0), .out(multiplexer_1_out));
  _4_Bit_PC_Adder _4_bit_pc_adder_1 (.I_3_0(_4_bit_program_counter_1_o_3_0), .O_3_0(_4_bit_pc_adder_1_o_3_0));
  _4_Bit_Program_Counter _4_bit_program_counter_1 (
    .I_3_0(multiplexer_1_out), .CLK(CPU_CLK), .O_3_0(_4_bit_program_counter_1_o_3_0));
  and and_1 (CPU_CLK, PC_EN, CLK);
  _9X15_SRAM _9x15_sram_1 (
    .RA1_3_0(_4_bit_program_counter_1_o_3_0), .RA2_3_0(RA2_3_0), .WR_3_0(WR_3_0), .WRD_14_0(WRD_14_0),
    .WE(WE), .CLK(CLK), .RD1_14_0({_9x15_sram_1_rd1_14_0, JMP_ADDR_3_0, R2_2_0[1:0], Don_t_Care}),
    .RD2_14_0(RD2_14_0));
  _3_Bit_CU _3_bit_cu_1 (
    .Opcode_3_0(_9x15_sram_1_rd1_14_0), .ZF(ZF), .SF(SF), .Op_1_0(Op), .WE(REG_EN), .Imm_Sel(IMM_Sel),
    .Jmp_Sel(JMP_SEL));
  _3_Bit_Register_Set _3_bit_register_set_1 (
    .WR_2_0(JMP_ADDR_3_0[3:1]), .CLK(CPU_CLK), .A_2_0(A_2_0), .B_2_0(_3_bit_register_set_1_b_2_0),
    .RA_2_0(JMP_ADDR_3_0[3:1]), .RB_2_0({JMP_ADDR_3_0[0], R2_2_0[1:0]}), .WE(REG_EN), .WRD_2_0(R_2_0));
  _3_Bit_ALU _3_bit_alu_1 (.A_2_0(A_2_0), .B_2_0(B_2_0), .OP_1_0(Op), .R_2_0(R_2_0));
  Multiplexer #(.Bits(3)) multiplexer_2 (
    .sel(IMM_Sel), .in_0(_3_bit_register_set_1_b_2_0), .in_1({JMP_ADDR_3_0[0], R2_2_0[1:0]}), .out(B_2_0));

  assign R1_2_0 = JMP_ADDR_3_0[3:1];
  assign R2_2_0[2] = JMP_ADDR_3_0[0];
  assign WR_2_0 = JMP_ADDR_3_0[3:1];

  // Other names for the same wires on the sheet: R2[2:0] = {JMP_ADDR_3_0[0], R2_2_0[1:0]};
  //   JMP_ADDR[3:0] = JMP_ADDR_3_0; R1[2:0] = JMP_ADDR_3_0[3:1]; A[2:0] = A_2_0; B[2:0] = B_2_0; R[2:0] = R_2_0;
  //   RD2[14:0] = RD2_14_0

  // Notes on the sheet:
  //   Register Mode (Type of Op = 00 ) = 2 bit (Type of Op) + 2 bit (Op) + 3 bit (R1) + 3 bit (R2) + 5 bit (Don't Care)
  //   Immediate Mode (Type of Op = 01 ) = 2 bit (Type of Op) + 2 bit (Op) + 3 bit (R1) + 3 bit (Imm Value) + 5 bit (Don't Care)
  //   Jump Mode (Type of Op = 10 ) = 2 bit (Type of Op) + 2 bit (Op) + 4 bit (Address) + 7 bit (Don't Care)
  //   Add (Op = 00)             OR (Op = 01)              ROL(Op = 10)
  //   JMP (Op = 00),          JGE (Op = 01)
  //   JGE START  -->> 100100010000000
  //   START:  OR R1,R1  -->> 000100100100000
  //   JMP_TO: ADD R1,5  -->> 010000110100000
  //   JMP JMP_TO  -->> 100000100000000
endmodule
