// Digital circuit 3 Bit CU.dig as structural Verilog
module _3_Bit_CU (
  input  [3:0] Opcode_3_0,
  input  ZF,
  input  SF,
  output [1:0] Op_1_0,
  output WE,
  output Imm_Sel,
  output Jmp_Sel
);

  wire and_1_out, and_3_out, and_4_out, and_5_out, or_1_out, or_3_out;

  or or_1 (or_1_out, ZF, ~SF);  // Or
  and and_1 (and_1_out, ~Opcode_3_0[2], ~Opcode_3_0[3]);  // And
  and and_2 (Imm_Sel, Opcode_3_0[2], ~Opcode_3_0[3]);  // And
  and and_3 (and_3_out, ~Opcode_3_0[2], Opcode_3_0[3]);  // And
  and and_4 (and_4_out, ~Opcode_3_0[0], ~Opcode_3_0[1]);  // And
  and and_5 (and_5_out, Opcode_3_0[0], ~Opcode_3_0[1], or_1_out);  // And
  or or_2 (WE, and_1_out, Imm_Sel);
  or or_3 (or_3_out, and_4_out, and_5_out);
  and and_6 (Jmp_Sel, and_3_out, or_3_out);

  assign Op_1_0 = Opcode_3_0[1:0];
endmodule
