// Digital circuit 3 Bit OR.dig as structural Verilog
module _3_Bit_OR (
  input  [2:0] A_2_0,
  input  [2:0] B_2_0,
  output [2:0] R_2_0
);

  or or_1 (R_2_0[0], A_2_0[0], B_2_0[0]);
  or or_2 (R_2_0[1], A_2_0[1], B_2_0[1]);
  or or_3 (R_2_0[2], A_2_0[2], B_2_0[2]);

  // Other names for the same wires on the sheet: A0 = A_2_0[0]; A1 = A_2_0[1]; A2 = A_2_0[2]; B0 = B_2_0[0];
  //   B1 = B_2_0[1]; B2 = B_2_0[2]; R0 = R_2_0[0]; R1 = R_2_0[1]; R2 = R_2_0[2]
endmodule
