// Digital circuit 3 Bit Register Set.dig as structural Verilog
module _3_Bit_Register_Set (
  input  CLK,
  input  [2:0] RA_2_0,
  input  [2:0] RB_2_0,
  input  [2:0] WR_2_0,
  input  WE,
  input  [2:0] WRD_2_0,
  output [2:0] A_2_0,
  output [2:0] B_2_0
);

  wire A0, A1, A2, A3, A4, A5, D0, D1, D2, D3, D4, D5;
  wire [2:0] R0, R1, R2, R3, R4, R5;

  and and_1 (D0, A0, WE);
  and and_2 (D3, A3, WE);
  and and_3 (D1, A1, WE);
  and and_4 (D4, A4, WE);
  Decoder #(.Selector_Bits(3)) decoder_1 (
    .sel(WR_2_0), .out_0(A0), .out_1(A1), .out_2(A2), .out_3(A3), .out_4(A4), .out_5(A5));  // open: out_6, out_7
  and and_5 (D2, A2, WE);
  and and_6 (D5, A5, WE);
  _3_Bit_Register _3_bit_register_1 (.Din_2_0(WRD_2_0), .Sel(D5), .CLK(CLK), .Dout_2_0(R5));
  _3_Bit_Register _3_bit_register_2 (.Din_2_0(WRD_2_0), .Sel(D4), .CLK(CLK), .Dout_2_0(R4));
  _3_Bit_Register _3_bit_register_3 (.Din_2_0(WRD_2_0), .Sel(D3), .CLK(CLK), .Dout_2_0(R3));
  _3_Bit_Register _3_bit_register_4 (.Din_2_0(WRD_2_0), .Sel(D2), .CLK(CLK), .Dout_2_0(R2));
  _3_Bit_Register _3_bit_register_5 (.Din_2_0(WRD_2_0), .Sel(D1), .CLK(CLK), .Dout_2_0(R1));
  _3_Bit_Register _3_bit_register_6 (.Din_2_0(WRD_2_0), .Sel(D0), .CLK(CLK), .Dout_2_0(R0));
  Multiplexer #(.Selector_Bits(3), .Bits(3)) multiplexer_1 (
    .sel(RA_2_0), .in_0(R0), .in_1(R1), .in_2(R2), .in_3(R3), .in_4(R4), .in_5(R5), .in_6(3'b000),
    .in_7(3'b000), .out(A_2_0));
  Multiplexer #(.Selector_Bits(3), .Bits(3)) multiplexer_2 (
    .sel(RB_2_0), .in_0(R0), .in_1(R1), .in_2(R2), .in_3(R3), .in_4(R4), .in_5(R5), .in_6(3'b000),
    .in_7(3'b000), .out(B_2_0));
endmodule
