// Digital circuit 3 Bit Register.dig as structural Verilog
module _3_Bit_Register (
  input  [2:0] Din_2_0,
  input  CLK,
  input  Sel,
  output [2:0] Dout_2_0
);

  _1_Bit_Register _1_bit_register_1 (.Dout(Dout_2_0[2]), .Din(Din_2_0[2]), .Sel(Sel), .CLK(CLK));
  _1_Bit_Register _1_bit_register_2 (.Dout(Dout_2_0[1]), .Din(Din_2_0[1]), .Sel(Sel), .CLK(CLK));
  _1_Bit_Register _1_bit_register_3 (.Dout(Dout_2_0[0]), .Din(Din_2_0[0]), .Sel(Sel), .CLK(CLK));

  // Other names for the same wires on the sheet: B0 = Dout_2_0[0]; B1 = Dout_2_0[1]; B2 = Dout_2_0[2];
  //   A0 = Din_2_0[0]; A1 = Din_2_0[1]; A2 = Din_2_0[2]
endmodule
