// Digital circuit 4 Bit Program Counter.dig as structural Verilog
module _4_Bit_Program_Counter (
  input  [3:0] I_3_0,
  input  CLK,
  output [3:0] O_3_0
);

  _1_Bit_Register _1_bit_register_1 (.Dout(O_3_0[0]), .Din(I_3_0[0]), .Sel(1'b1), .CLK(CLK));
  _3_Bit_Register _3_bit_register_1 (.Din_2_0(I_3_0[3:1]), .Sel(1'b1), .CLK(CLK), .Dout_2_0(O_3_0[3:1]));

  // Other names for the same wires on the sheet: B0 = O_3_0[0]; B1[2:0] = O_3_0[3:1]; A0 = I_3_0[0];
  //   A1[2:0] = I_3_0[3:1]
endmodule
